// Logisim project CicloFetchDecoderExecute.circ as structural Verilog: 1 circuit, main circuit main
module main (
  input  PincC,
  input  PinA,
  input  PinB
);

  wire and_1_out, and_2_out, AND_JUMP_out, AND_STORE_out, clock_1_out, decoder_1_out1, decoder_1_out2,
       decoder_1_out3, decoder_1_out4, not_1_out, or_1_out, or_2_out;
  wire [3:0] adder_2_out, MAR_q, multiplexer_1_out, multiplexer_2_out, PC_q;
  wire [7:0] AC_q, adder_1_out, IR_q, MDR_q, multiplexer_3_out, ram_1_data;

  Clock clock_1 (.out(clock_1_out));
  Adder adder_1 (.a(AC_q), .b(MDR_q), .out(adder_1_out), .cin(1'b0));  // open: cout
  Register #(.width(4)) PC (.D(multiplexer_1_out), .en(or_1_out), .Q(PC_q), .clk(clock_1_out), .clr(1'b0));
  Register IR (.D(MDR_q), .en(not_1_out), .Q(IR_q), .clk(clock_1_out), .clr(1'b0));
  Multiplexer #(.width(4)) multiplexer_1 (
    .in0(adder_2_out), .in1(IR_q[3:0]), .out(multiplexer_1_out), .sel(AND_JUMP_out));  // open: en
  Adder #(.width(4)) adder_2 (.a(PC_q), .b(4'b0001), .out(adder_2_out));  // open: cin, cout
  Register #(.width(4)) MAR (.D(multiplexer_2_out), .en(1'b1), .Q(MAR_q), .clk(clock_1_out), .clr(1'b0));
  Multiplexer #(.width(4)) multiplexer_2 (
    .in0(PC_q), .in1(IR_q[3:0]), .out(multiplexer_2_out), .sel(PinA));  // open: en
  not not_1 (not_1_out, PinA);
  Register AC (.D(multiplexer_3_out), .en(or_2_out), .Q(AC_q), .clk(clock_1_out), .clr(1'b0));
  Register MDR (.D(ram_1_data), .en(1'b1), .Q(MDR_q), .clk(clock_1_out), .clr(1'b0));
  Multiplexer #(.width(8), .enable("false")) multiplexer_3 (
    .in0(MDR_q), .in1(adder_1_out), .out(multiplexer_3_out), .sel(and_2_out));
  RAM #(.addrWidth(4), .bus("separate")) ram_1 (
    .addr(MAR_q), .din(AC_q), .data(ram_1_data), .str(AND_STORE_out), .sel(1'b1), .clk(clock_1_out),
    .ld(1'b1), .clr(1'b0));
  // Probe on MDR_q
  Decoder #(.select(4)) decoder_1 (
    .out1(decoder_1_out1), .out2(decoder_1_out2), .out3(decoder_1_out3), .out4(decoder_1_out4),
    .sel(IR_q[7:4]), .en(1'b1));  // open: out0, out5, out6, out7, out8, out9, out10, out11, out12, out13, out14, out15
  and and_1 (and_1_out, decoder_1_out2, PinB);
  or or_1 (or_1_out, PincC, AND_JUMP_out);
  LED ADD (.in(decoder_1_out1));
  LED LOAD (.in(decoder_1_out2));
  LED STORE (.in(decoder_1_out3));
  LED JUMP (.in(decoder_1_out4));
  and and_2 (and_2_out, decoder_1_out1, PinB);
  and AND_STORE (AND_STORE_out, decoder_1_out3, PinB);
  or or_2 (or_2_out, and_2_out, and_1_out);
  and AND_JUMP (AND_JUMP_out, decoder_1_out4, PinB);
endmodule
